# Fritzing sketch reverse gear (saved by Fritzing 0.9.4)
breadboards: 1

parts:
  Part1 = Arduino Uno (Rev3)
  LED1 = LED - 5mm [color="Red (633nm)" package="5 mm [THT]"]
  HC-SR04_Sensor_1 = HC-SR04 Ultrasonic Distance Sensor
  R1 = Resistor [tolerance=±5% resistance=220 package=THT]

nets:
  N1: Part1.D9_PWM, HC-SR04_Sensor_1.ECHO
  N2: Part1.D10_PWM/SS, HC-SR04_Sensor_1.TRIG
  N3: Part1.D11_PWM/MOSI, LED1.cathode
  GND: Part1.GND, HC-SR04_Sensor_1.GND, R1.Pin_1
  5V: Part1.5V, HC-SR04_Sensor_1.VCC
  N4: LED1.anode, R1.Pin_0
